# Fritzing sketch lamp_effect (saved by Fritzing 0.9.4)
breadboards: 1

parts:
  Part1 = Arduino Nano (Rev3.0)
  LED1 = LED - 3mm [color="Red (633nm)" package="3 mm [THT]"]
  R1 = Resistor [tolerance=±5% resistance=1k package="0402 [SMD]"]

nets:
  N1: Part1.D4, LED1.anode
  VIN: Part1.VIN, Part1.GND, R1.Pin_0
  N2: LED1.cathode, R1.Pin_1
